# Fritzing sketch EsquematicoProjeto (saved by Fritzing 0.9.3b)
breadboards: 1

parts:
  DS1 = DS18B20 1-Wire Temperature Sensor Probe Cable
  Componente1 = Arduino Mega 2560 (Rev3)
  LED1 = LED - 5mm [color="Red (633nm)" package="5 mm [THT]"]
  R1 = Resistor [tolerance=±5% resistance=100 package=THT]
  R2 = Resistor [tolerance=±5% resistance=150 package=THT]
  R3 = Resistor [tolerance=±5% resistance=4.7k package=THT]
  S1 = Square Pushbutton

nets:
  GND: DS1.GND, Componente1.GND, LED1.cathode, R2.Pin_1
  VDD: DS1.VDD, Componente1.5V, R3.Pin_0, S1.leg1
  N1: DS1.shield, Componente1.D13_PWM, R3.Pin_1
  N2: Componente1.D12_PWM, R2.Pin_0, S1.leg0
  N3: Componente1.D11_PWM, LED1.anode, R1.Pin_0, R1.Pin_1
